# Fritzing sketch joystick-wiring (saved by Fritzing 0.9.3b)

parts:
  Part1 = Arduino Pro Mini v13
  HC-1 = HC-12 Module
  Part2 = Thumb Joystick

nets:
  GND: Part1.GND, HC-1.GND, Part2.GND
  VCC: Part1.VCC, HC-1.VCC, Part2.VCC
  N1: Part1.A1, Part2.HORZ
  N2: Part1.A0, Part2.VERT
  N3: Part1.D12/MISO, HC-1.SET
  N4: Part1.D11_PWM/MOSI, HC-1.RXD
  N5: Part1.D10_PWM/SS, HC-1.TXD

custom parts:
  HC-12 Module: HC-12 433Mhz Module
