# Fritzing sketch tank-wiring (saved by Fritzing 0.9.3b)
breadboards: 1

parts:
  Part1 = Arduino Nano (Rev3.0)
  HC-1 = HC-12 Module
  M1 = DC Motor
  M2 = DC Motor
  L298N2 = L298N DC motor driver
  M4 = DC Motor
  M5 = DC Motor

nets:
  N1: Part1.D3, L298N2.IN4
  N2: Part1.D5, L298N2.IN3
  N3: Part1.D6, L298N2.IN2
  N4: Part1.D9, L298N2.IN1
  N5: Part1.D10, HC-1.TXD
  N6: Part1.D11/MOSI, HC-1.RXD
  N7: Part1.D12/MISO, HC-1.SET
  5V: Part1.5V, HC-1.VCC
  GND: HC-1.GND, L298N2.GND
  N8: M1.pin_1, L298N2.OUT4, M5.pin_1
  N9: M1.pin_2, L298N2.OUT3, M5.pin_2
  N10: M2.pin_1, L298N2.OUT2, M4.pin_1
  N11: M2.pin_2, L298N2.OUT1, M4.pin_2
  N12: L298N2.5V#9, L298N2.ENA
  N13: L298N2.5V#10, L298N2.ENB

notes:
  right motors
  left motors

custom parts:
  HC-12 Module: HC-12 433Mhz Module
  L298N DC motor driver: 2x DC motor driver with 78M05 positive voltage regulator (7..35 V) L298N: max 46 V, 2 A Set 5 V Enable jumper to enable 5 V regultor (needed for the L298N) and +5 V output at screw terminal or supply external +5 V at screw terminal Set ENA and/or ENB to +5 V to enable motor permanently or supply ENA and/or ENB with PWM signal IN1 and IN2 set rotation directory for motor A (OUT1/OUT2) IN2 and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
